# Fritzing sketch course 7 (saved by Fritzing 1.0.5)
breadboards: 1

parts:
  SEN1 = US-100 Ultrasonic Distance Sensor
  Part1 = Arduino Uno (Rev3)

nets:
  VCC: SEN1.VCC, Part1.5V
  N1: SEN1.TRIG, Part1.D11_PWM/MOSI
  N2: SEN1.ECHO, Part1.D12/MISO
  GND: SEN1.GND, SEN1.GND-2, Part1.GND
